// Logisim project F2.circ as structural Verilog: 1 circuit, main circuit main
module main (
  input  x,
  input  y,
  output out_3
);

  wire Adn2_out, And1_out, not_1_out, not_2_out;

  not not_1 (not_1_out, y);
  not not_2 (not_2_out, x);
  and And1 (And1_out, x, not_1_out);
  and Adn2 (Adn2_out, not_2_out, y);
  or Or1 (out_3, And1_out, Adn2_out);
endmodule
